// Logisim project CU.circ as structural Verilog: 2 circuits, main circuit main
// CU
module main (
  input  [15:0] Instruction,
  output [3:0] COM,
  output [2:0] A1,
  output [2:0] A2,
  output [7:0] MA
);

  // PARSER parser_1: pin names not known; wires that end beside it: Instruction, COM, A1, A2, MA
endmodule

// PAR
module PARSER (
  input  [15:0] Instruction,
  output [3:0] COMMAND,
  output [2:0] A1,
  output [2:0] A2,
  output [7:0] M1
);


  assign A1 = Instruction[6:4];
  assign A2 = Instruction[9:7];
  assign COMMAND = Instruction[3:0];
  assign M1 = Instruction[11:4];
endmodule
