// Logisim project procesor.circ as structural Verilog
module Procesor (
  input  [15:0] in_1,
  input  LD,
  input  [15:0] in_3,
  output [15:0] out_4,
  output [7:0] out_5,
  output [7:0] out_6
);

  wire CLK_out, main_1_mov, main_1_s_l, not_1_out;
  wire [2:0] main_1_a1, main_1_a2, main_1_a_input;
  wire [3:0] main_1_com;
  wire [7:0] MEM, ram_2_data, registers_1_value1, registers_1_value2;

  Clock CLK (.out(CLK_out));
  CU_main main_1 (
    .Instruction(in_3), .COM(main_1_com), .A1(main_1_a1), .A2(main_1_a2), .MA(MEM), .A_Input(main_1_a_input),
    .S_L(main_1_s_l), .MOV(main_1_mov));
  not not_1 (not_1_out, main_1_s_l);
  RAM #(.dataWidth(16), .bus("separate")) ram_1 (
    .din(in_1), .data(out_4), .clk(CLK_out), .ld(LD));  // open: addr, str, sel, clr
  Registers registers_1 (
    .DESTINATION(main_1_a2), .VALUE1(registers_1_value1), .CLK(CLK_out), .SOURCE1(main_1_a1),
    .in_7(not_1_out), .MEM(ram_2_data), .VALUE2(registers_1_value2), .SOURCE2(main_1_a_input), .AX(out_6),
    .in_2(main_1_mov));
  RAM #(.bus("separate")) ram_2 (
    .addr(MEM), .din(out_6), .data(ram_2_data), .str(main_1_s_l), .clk(CLK_out), .ld(not_1_out));  // open: sel, clr
  ALU alu_1 (
    .R1__Value_of_first_register(registers_1_value1), .R2__Value_of_second_register(registers_1_value2),
    .OUT__ALU_output(out_5), .COM__Value_of_command__0000_to_1111(main_1_com));  // open: FLAGS_ZCOP

  // Other names for the same wires on the sheet: AX[7:0] = out_6

  // Notes on the sheet:
  //   INSTRUCTIONS
  //   DATA
endmodule
